// Logisim project multiplexer.circ as structural Verilog: 2 circuits, main circuit main
module main (
  input  S,
  input  A0,
  input  A1,
  input  A2,
  input  A3,
  input  B0,
  input  B1,
  input  B2,
  input  B3,
  output Z0,
  output Z1,
  output Z2,
  output Z3
);

  mux2 mux2_1 (.S(S), .A0(A0), .A1(A1), .B0(B0), .B1(B1), .Z0(Z0), .Z1(Z1));
  mux2 mux2_2 (.S(S), .A0(A2), .A1(A3), .B0(B2), .B1(B3), .Z0(Z2), .Z1(Z3));
endmodule

module mux2 (
  input  S,
  input  A0,
  input  A1,
  input  B0,
  input  B1,
  output Z0,
  output Z1
);

  wire U1_out, U2_out, U3_out, U4_out, U5_out;

  not U5 (U5_out, S);
  and U1 (U1_out, A0, U5_out);
  and U2 (U2_out, A1, U5_out);
  and U3 (U3_out, B0, S);
  and U4 (U4_out, B1, S);
  or U6 (Z0, U1_out, U3_out);
  or U7 (Z1, U2_out, U4_out);
endmodule
