// Logisim project parallel_signed_4-bit_comparator.circ as structural Verilog: 1 circuit, main circuit main
module main (
  input  A3,
  input  A2,
  input  A1,
  input  A0,
  input  B3,
  input  B2,
  input  B1,
  input  B0,
  output A_B,
  output A_B_2,
  output A_B_3
);

  wire and_1_out, and_2_out, and_3_out, and_4_out, and_5_out, and_6_out, comparator_1_eq, comparator_1_gt,
       comparator_1_lt, comparator_2_eq, comparator_2_gt, comparator_2_lt, comparator_3_eq, comparator_3_gt,
       comparator_3_lt, comparator_4_eq, comparator_4_gt, comparator_4_lt, not_1_out, not_2_out;

  not not_1 (not_1_out, A3);
  Comparator #(.width(1), .mode("unsigned")) comparator_1 (
    .a(not_1_out), .b(not_2_out), .gt(comparator_1_gt), .eq(comparator_1_eq), .lt(comparator_1_lt));
  not not_2 (not_2_out, B3);
  Comparator #(.width(1), .mode("unsigned")) comparator_2 (
    .a(A2), .b(B2), .gt(comparator_2_gt), .eq(comparator_2_eq), .lt(comparator_2_lt));
  Comparator #(.width(1), .mode("unsigned")) comparator_3 (
    .a(A1), .b(B1), .gt(comparator_3_gt), .eq(comparator_3_eq), .lt(comparator_3_lt));
  Comparator #(.width(1), .mode("unsigned")) comparator_4 (
    .a(A0), .b(B0), .gt(comparator_4_gt), .eq(comparator_4_eq), .lt(comparator_4_lt));
  and and_1 (and_1_out, comparator_1_eq, comparator_2_gt);
  and and_2 (and_2_out, comparator_1_eq, comparator_2_lt);
  and and_3 (and_3_out, comparator_1_eq, comparator_2_eq, comparator_3_gt);
  and and_4 (and_4_out, comparator_1_eq, comparator_2_eq, comparator_3_lt);
  and and_5 (and_5_out, comparator_1_eq, comparator_2_eq, comparator_3_eq, comparator_4_gt);
  and and_6 (and_6_out, comparator_1_eq, comparator_2_eq, comparator_3_eq, comparator_4_lt);
  or or_1 (A_B, comparator_1_gt, and_1_out, and_3_out, and_5_out);
  and and_7 (A_B_2, comparator_1_eq, comparator_2_eq, comparator_3_eq, comparator_4_eq);
  or or_2 (A_B_3, comparator_1_lt, and_2_out, and_4_out, and_6_out);
endmodule
