// Logisim project serial_signed_4-bit_comparator.circ as structural Verilog: 2 circuits, main circuit main
module main (
  input  A0,
  input  A1,
  input  A2,
  input  A3,
  input  B0,
  input  B1,
  input  B2,
  input  B3,
  output A_B,
  output A_B_2,
  output A_B_3
);

  wire cmp1_1_a_b_4, cmp1_1_a_b_5, cmp1_1_a_b_6, cmp1_2_a_b_4, cmp1_2_a_b_5, cmp1_2_a_b_6, cmp1_3_a_b_4,
       cmp1_3_a_b_5, cmp1_3_a_b_6, not_1_out, not_2_out;

  not not_1 (not_1_out, A3);
  not not_2 (not_2_out, B3);
  cmp1 cmp1_1 (
    .A(A0), .B(B0), .A_B(1'b0), .A_B_2(1'b0), .A_B_3(1'b0), .A_B_4(cmp1_1_a_b_4), .A_B_5(cmp1_1_a_b_5),
    .A_B_6(cmp1_1_a_b_6));
  cmp1 cmp1_2 (
    .A(A1), .B(B1), .A_B(cmp1_1_a_b_4), .A_B_2(cmp1_1_a_b_5), .A_B_3(cmp1_1_a_b_6), .A_B_4(cmp1_2_a_b_4),
    .A_B_5(cmp1_2_a_b_5), .A_B_6(cmp1_2_a_b_6));
  cmp1 cmp1_3 (
    .A(A2), .B(B2), .A_B(cmp1_2_a_b_4), .A_B_2(cmp1_2_a_b_5), .A_B_3(cmp1_2_a_b_6), .A_B_4(cmp1_3_a_b_4),
    .A_B_5(cmp1_3_a_b_5), .A_B_6(cmp1_3_a_b_6));
  cmp1 cmp1_4 (
    .A(not_1_out), .B(not_2_out), .A_B(cmp1_3_a_b_4), .A_B_2(cmp1_3_a_b_5), .A_B_3(cmp1_3_a_b_6),
    .A_B_4(A_B), .A_B_5(A_B_2), .A_B_6(A_B_3));
endmodule

module cmp1 (
  input  A,
  input  B,
  input  A_B,
  input  A_B_2,
  input  A_B_3,
  output A_B_4,
  output A_B_5,
  output A_B_6
);

  wire and_1_out, and_2_out, not_1_out, not_2_out, not_3_out, not_4_out, xnor_1_out;

  not not_1 (not_1_out, A_B);
  not not_2 (not_2_out, A_B_3);
  not not_3 (not_3_out, B);
  xnor xnor_1 (xnor_1_out, A, B);
  not not_4 (not_4_out, A);
  and and_1 (and_1_out, A, not_3_out);
  and and_2 (and_2_out, not_4_out, B);
  and and_3 (A_B_5, xnor_1_out, not_1_out, not_2_out);
  or or_1 (A_B_4, and_2_out, A_B);
  or or_2 (A_B_6, and_1_out, A_B_3);
endmodule
