// Logisim project alu.circ as structural Verilog: 1 circuit, main circuit main
module main (
  input  [2:0] aluc,
  input  [31:0] A,
  input  cin_add,
  input  cin_sub,
  input  [31:0] B,
  output [31:0] alu_out,
  output zero,
  output over
);

  wire _001_out, _011_out, _100_out, _110_out, bitselector_1_out, bitselector_2_out, bitselector_3_out,
       or_2_out, or_3_out;
  wire [31:0] adder_1_out, And_out, Or_out, subtractor_1_out;

  Adder #(.width(32)) adder_1 (.a(A), .b(B), .out(adder_1_out), .cin(cin_add));  // open: cout
  Subtractor #(.width(32)) subtractor_1 (.a(A), .b(A), .out(subtractor_1_out), .bin(cin_sub));  // open: bout
  assign Or_out = A | B;  // OR_Gate Or, 32 bits wide
  assign And_out = A & B;  // AND_Gate And, 32 bits wide
  BitSelector #(.width(32)) bitselector_1 (.in(A), .out(bitselector_1_out), .sel({5{1'b1}}));
  BitSelector #(.width(32)) bitselector_2 (.in(B), .out(bitselector_2_out), .sel({5{1'b1}}));
  BitSelector #(.width(32)) bitselector_3 (.in(alu_out), .out(bitselector_3_out), .sel({5{1'b1}}));
  Multiplexer #(.select(3), .width(32), .enable("false")) multiplexer_1 (
    .in0(adder_1_out), .in1(subtractor_1_out), .in2(Or_out), .in3(And_out), .in4({32{1'b0}}),
    .in6({32{1'b0}}), .in7({32{1'b0}}), .out(alu_out), .sel(aluc));  // open: in5
  and _110 (_110_out, bitselector_1_out, bitselector_2_out, ~bitselector_3_out);  // AND_Gate
  or or_2 (or_2_out, _110_out, _001_out);
  and _001 (_001_out, ~bitselector_1_out, ~bitselector_2_out, bitselector_3_out);  // AND_Gate
  and _011 (_011_out, ~bitselector_1_out, bitselector_2_out, bitselector_3_out);  // AND_Gate
  or or_3 (or_3_out, _011_out, _100_out);
  and _100 (_100_out, bitselector_1_out, ~bitselector_2_out, ~bitselector_3_out);  // AND_Gate
  Comparator #(.width(32)) comparator_1 (.a(alu_out), .b({32{1'b0}}), .eq(zero));  // open: gt, lt
  Multiplexer #(.select(3), .enable("false")) multiplexer_2 (
    .in0(or_2_out), .in1(or_3_out), .in2(1'b0), .in3(1'b0), .in4(1'b0), .in5(1'b0), .in6(1'b0), .in7(1'b0),
    .out(over), .sel(aluc));
endmodule
