// Logisim project register-file.circ as structural Verilog: 1 circuit, main circuit main
module main (
  input  [7:0] rd,
  input  we,
  input  [2:0] ra,
  input  [2:0] rb,
  input  [2:0] rw,
  input  reset,
  output [7:0] out_7,
  output [7:0] qa,
  output [7:0] qb
);

  wire and_1_out, and_2_out, and_3_out, and_4_out, and_5_out, and_6_out, and_7_out, and_8_out, clk_out,
       decoder_1_out0, decoder_1_out1, decoder_1_out2, decoder_1_out3, decoder_1_out4, decoder_1_out5,
       decoder_1_out6, decoder_1_out7, not_1_out, or_1_out, or_2_out, or_3_out, or_4_out, or_5_out, or_6_out,
       or_7_out, or_8_out;
  wire [7:0] r0_q, r1_q, r2_q, r3_q, r4_q, r5_q, r6_q, r7_q;

  Decoder #(.select(3), .enable("false")) decoder_1 (
    .out0(decoder_1_out0), .out1(decoder_1_out1), .out2(decoder_1_out2), .out3(decoder_1_out3),
    .out4(decoder_1_out4), .out5(decoder_1_out5), .out6(decoder_1_out6), .out7(decoder_1_out7), .sel(rw));
  Clock clk (.out(clk_out));
  Multiplexer #(.width(8), .enable("false")) multiplexer_1 (.in0(rd), .in1({8{1'b0}}), .out(out_7), .sel(not_1_out));
  and and_1 (and_1_out, decoder_1_out0, we);
  and and_2 (and_2_out, decoder_1_out1, we);
  and and_3 (and_3_out, decoder_1_out2, we);
  and and_4 (and_4_out, decoder_1_out3, we);
  and and_5 (and_5_out, decoder_1_out4, we);
  and and_6 (and_6_out, decoder_1_out5, we);
  and and_7 (and_7_out, decoder_1_out6, we);
  and and_8 (and_8_out, decoder_1_out7, we);
  not not_1 (not_1_out, reset);
  or or_1 (or_1_out, and_1_out, not_1_out);
  or or_2 (or_2_out, and_2_out, not_1_out);
  or or_3 (or_3_out, and_3_out, not_1_out);
  or or_4 (or_4_out, and_4_out, not_1_out);
  or or_5 (or_5_out, and_5_out, not_1_out);
  or or_6 (or_6_out, and_6_out, not_1_out);
  or or_7 (or_7_out, and_7_out, not_1_out);
  or or_8 (or_8_out, and_8_out, not_1_out);
  Register r0 (.D(out_7), .en(or_1_out), .Q(r0_q), .clk(clk_out));  // open: clr
  Register r4 (.D(out_7), .en(or_5_out), .Q(r4_q), .clk(clk_out));  // open: clr
  Register r1 (.D(out_7), .en(or_2_out), .Q(r1_q), .clk(clk_out));  // open: clr
  Register r2 (.D(out_7), .en(or_3_out), .Q(r2_q), .clk(clk_out));  // open: clr
  Register r6 (.D(out_7), .en(or_7_out), .Q(r6_q), .clk(clk_out));  // open: clr
  Register r5 (.D(out_7), .en(or_6_out), .Q(r5_q), .clk(clk_out));  // open: clr
  Register r3 (.D(out_7), .en(or_4_out), .Q(r3_q), .clk(clk_out));  // open: clr
  Register r7 (.D(out_7), .en(or_8_out), .Q(r7_q), .clk(clk_out));  // open: clr
  Multiplexer #(.select(3), .width(8), .enable("false")) multiplexer_2 (
    .in0(r0_q), .in1(r1_q), .in2(r2_q), .in3(r3_q), .in4(r4_q), .in5(r5_q), .in6(r6_q), .in7(r7_q), .out(qa),
    .sel(ra));
  Multiplexer #(.select(3), .width(8), .enable("false")) multiplexer_3 (
    .in0(r0_q), .in1(r1_q), .in2(r2_q), .in3(r3_q), .in4(r4_q), .in5(r5_q), .in6(r6_q), .in7(r7_q), .out(qb),
    .sel(rb));
endmodule
